# Fritzing sketch schaltplan (saved by Fritzing 0.9.3b)
circuit board: 7.1356cm x 5.52797cm
breadboards: 1

parts:
  S1 = Pushbutton [package="[THT]"]
  R1 = Resistor [tolerance=±5% resistance=10k package=THT]
  LED1 = LED - 5mm [color="Red (633nm)" package="5 mm [THT]"]
  LED2 = LED - 5mm [color="Yellow (592nm)" package="5 mm [THT]"]
  LED3 = LED - 5mm [color="Green (570nm)" package="5 mm [THT]"]
  LED4 = LED - 5mm [color="Red (633nm)" package="5 mm [THT]"]
  LED5 = LED - 5mm [color="Green (570nm)" package="5 mm [THT]"]
  R2 = Resistor [tolerance=±5% resistance=150 package=THT]
  R3 = Resistor [tolerance=±5% resistance=150 package=THT]
  R4 = Resistor [tolerance=±5% resistance=150 package=THT]
  R5 = Resistor [tolerance=±5% resistance=150 package=THT]
  R6 = Resistor [tolerance=±5% resistance=150 package=THT]
  Bauteil1 = Arduino Uno (Rev3)
  J1 = female pin header, 4 pins [form="♀ (female)"]
  J1_2 = female pin header, 4 pins [form="♀ (female)"]

nets:
  N1: S1.Pin_1, S1.Pin_2, Bauteil1.5V, J1.pin4, J1_2.pin4
  N2: S1.Pin_3, S1.Pin_4, R1.Pin_1, Bauteil1.D4
  N3: R1.Pin_0, R2.Pin_0, R3.Pin_0, R4.Pin_0, R5.Pin_0, R6.Pin_0, Bauteil1.GND, J1.pin1, J1_2.pin1
  N4: LED1.cathode, R6.Pin_1
  N5: LED1.anode, Bauteil1.D3_PWM
  N6: LED2.cathode, R5.Pin_1
  N7: LED2.anode, Bauteil1.D5_PWM
  N8: LED3.cathode, R4.Pin_1
  N9: LED3.anode, Bauteil1.D6_PWM
  N10: LED4.cathode, R3.Pin_1
  N11: LED4.anode, Bauteil1.D9_PWM
  N12: LED5.cathode, R2.Pin_1
  N13: LED5.anode, Bauteil1.D10_PWM/SS
  N14: Bauteil1.D0/RX, J1.pin3, J1_2.pin3
  N15: Bauteil1.D1/TX, J1.pin2, J1_2.pin2
